// Logisim project hw4fsm.circ as structural Verilog: 1 circuit, main circuit main
module main (
  input  Input,
  input  Clock,
  output Output
);


  // Notes on the sheet:
  //   DO NOT MOVE GIVEN PINS
endmodule
