// Logisim project hw4fsm.circ as structural Verilog: 1 circuit, main circuit main
module main (
  input  Input,
  input  Clock,
  output Output
);

  wire and_1_out, and_2_out, d_ff_1_q, d_ff_2_q, not_1_out, not_2_out, or_1_out, or_2_out;

  not not_1 (not_1_out, d_ff_1_q);
  not not_2 (not_2_out, or_1_out);
  or or_1 (or_1_out, d_ff_1_q, d_ff_2_q);
  or or_2 (or_2_out, not_1_out, d_ff_2_q);
  and and_1 (and_1_out, not_2_out, Input);
  and and_2 (and_2_out, Input, or_2_out);
  D_Flip_Flop d_ff_1 (.clk(Clock), .D(and_1_out), .Q(d_ff_1_q));  // open: Qn, preset, en, reset
  D_Flip_Flop d_ff_2 (.clk(Clock), .D(and_2_out), .Q(d_ff_2_q));  // open: Qn, preset, en, reset
  and and_3 (Output, d_ff_1_q, Input, d_ff_2_q);

  // Notes on the sheet:
  //   DO NOT MOVE GIVEN PINS
endmodule
