// Logisim project lab10.circ as structural Verilog: 8 circuits, main circuit main
module main (
  input  [15:0] in_1,
  input  [3:0] in_2,
  output [15:0] out_3
);

  rotr rotr_1 (.A(in_1), .B(in_2), .Out(out_3));
endmodule

module Ex1 (
  input  [7:0] Input,
  input  [6:0] Inp2,
  output Out1,
  output [7:0] Out2
);

  and and_1 (Out1, Input[0], Input[7]);
  not not_1 (Out2[7], Input[7]);

  assign Out2[6:0] = Input[6:0];
endmodule

module rotr (
  input  [15:0] A,
  input  [3:0] B,
  output [15:0] Out
);

  wire [3:0] not_1_out;
  wire [15:0] multiplexer_1_out, multiplexer_2_out, multiplexer_3_out, n1_bit_shift_1_out_2,
       n2_bit_shift_1_out_2, n4_bit_shift_1_out_2, n8_bit_shift_1_out_2;

  _1_bit_shift u_1_bit_shift_1 (.unshift(A), .out_2(n1_bit_shift_1_out_2));
  Multiplexer #(.width(16)) multiplexer_1 (
    .in0(n1_bit_shift_1_out_2), .in1(A), .out(multiplexer_1_out), .sel(not_1_out[0]));  // open: en
  assign not_1_out = ~B;  // NOT_Gate not_1, 4 bits wide
  _2_bit_shift u_2_bit_shift_1 (.unshift(multiplexer_1_out), .out_2(n2_bit_shift_1_out_2));
  _4_bit_shift u_4_bit_shift_1 (.unshift(multiplexer_2_out), .out_2(n4_bit_shift_1_out_2));
  Multiplexer #(.width(16)) multiplexer_2 (
    .in0(n2_bit_shift_1_out_2), .in1(multiplexer_1_out), .out(multiplexer_2_out), .sel(not_1_out[1]));  // open: en
  _8_bit_shift u_8_bit_shift_1 (.unshift(multiplexer_3_out), .out_2(n8_bit_shift_1_out_2));
  Multiplexer #(.width(16)) multiplexer_3 (
    .in0(n4_bit_shift_1_out_2), .in1(multiplexer_2_out), .out(multiplexer_3_out), .sel(not_1_out[2]));  // open: en
  Multiplexer #(.width(16)) multiplexer_4 (
    .in0(n8_bit_shift_1_out_2), .in1(multiplexer_3_out), .out(Out), .sel(not_1_out[3]));  // open: en
endmodule

module fib (
);

  wire clock_1_out, comparator_1_eq, counter_1_q, counter_2_q, not_1_out;
  wire [15:0] adder_1_out, adder_2_out, multiplexer_1_out, multiplexer_2_out, register_1_q, register_2_q,
       register_3_q;

  Counter #(.width(1), .max('h1), .ongoal("stay")) counter_1 (
    .count(1'b1), .Q(counter_1_q), .clk(clock_1_out));  // open: load, D, carry, clr
  Clock clock_1 (.out(clock_1_out));
  Multiplexer #(.width(16), .enable("false")) multiplexer_1 (
    .in0({16{1'b0}}), .in1(register_1_q), .out(multiplexer_1_out), .sel(counter_2_q));
  Counter #(.width(1), .max('h1), .ongoal("stay")) counter_2 (
    .count(1'b1), .Q(counter_2_q), .clk(clock_1_out));  // open: load, D, carry, clr
  Multiplexer #(.width(16), .enable("false")) multiplexer_2 (
    .in0(16'h1), .in1(adder_1_out), .out(multiplexer_2_out), .sel(counter_1_q));
  Register #(.width(16)) register_1 (
    .D(multiplexer_2_out), .en(not_1_out), .Q(register_1_q), .clk(clock_1_out));  // open: clr
  Register #(.width(16)) register_2 (
    .D(multiplexer_1_out), .en(not_1_out), .Q(register_2_q), .clk(clock_1_out));  // open: clr
  Adder #(.width(16)) adder_1 (.a(register_1_q), .b(register_2_q), .out(adder_1_out));  // open: cin, cout
  Adder #(.width(16)) adder_2 (.a(register_3_q), .b(16'h1), .out(adder_2_out));  // open: cin, cout
  Register #(.width(16)) register_3 (
    .D(adder_2_out), .en(not_1_out), .Q(register_3_q), .clk(clock_1_out));  // open: clr
  Comparator #(.width(16)) comparator_1 (.a(register_3_q), .b(16'hf), .eq(comparator_1_eq));  // open: gt, lt
  // Probe on register_1_q
  not not_1 (not_1_out, comparator_1_eq);
endmodule

// 1 bit
module _1_bit_shift (
  input  [15:0] unshift,
  output [15:0] out_2
);


  assign out_2 = {unshift[0], unshift[15:1]};
endmodule

// 2 bit
module _2_bit_shift (
  input  [15:0] unshift,
  output [15:0] out_2
);


  assign out_2 = {unshift[1:0], unshift[15:2]};
endmodule

// 4 bit
module _4_bit_shift (
  input  [15:0] unshift,
  output [15:0] out_2
);


  assign out_2 = {unshift[3:0], unshift[15:4]};
endmodule

// 8 bit
module _8_bit_shift (
  input  [15:0] unshift,
  output [15:0] out_2
);


  assign out_2 = {unshift[7:0], unshift[15:8]};
endmodule
