// Logisim project lab11.circ as structural Verilog: 6 circuits, main circuit main
module main (
  input  [15:0] InpA,
  input  [15:0] InpB,
  input  [3:0] Select,
  output Signed,
  output UNSigned,
  output EQ,
  output [15:0] Result
);

  // ALU alu_1: pin names not known; wires that end beside it: InpA, InpB, Select, Signed, UNSigned, EQ, Result
endmodule

module ALU (
  input  [15:0] InpA,
  input  [15:0] Inp_B,
  input  [3:0] Selection,
  output UNSigned,
  output Equals,
  output [15:0] Result,
  output Signed_OF
);

  wire ArithSign, ArithUN, comparator_2_lt, PackedSign, PackedUN;
  wire [15:0] and_1_out, arith_1_result, bit_extender_1_out, or_1_out, packed_ops_1_result,
       shifter_1_shift_out;

  Comparator #(.width(16)) comparator_1 (.a(InpA), .b(Inp_B), .eq(Equals));  // open: gt, lt
  shifter shifter_1 (.InpA(InpA), .InpB(Inp_B), .OpSelect(Selection[1:0]), .Shift_Out(shifter_1_shift_out));
  arith arith_1 (
    .InpA(InpA), .InpB(Inp_B), .Opselect(Selection[0]), .\unsigned (ArithUN), .Result(arith_1_result),
    .Signed_Overflow(ArithSign));
  Comparator #(.width(16)) comparator_2 (.a(InpA), .b(Inp_B), .lt(comparator_2_lt));  // open: gt, eq
  assign or_1_out = InpA | Inp_B;  // OR_Gate or_1, 16 bits wide
  assign and_1_out = InpA & Inp_B;  // AND_Gate and_1, 16 bits wide
  packed_ops packed_ops_1 (
    .InpA(InpA), .Inp_B(Inp_B), .Selection(Selection[1:0]), .Result(packed_ops_1_result),
    .UNsigned(PackedUN), .Signed(PackedSign));
  assign bit_extender_1_out = {{15{1'b0}}, comparator_2_lt};  // Bit_Extender bit_extender_1
  Multiplexer #(.select(4), .width(16)) multiplexer_1 (
    .in0(arith_1_result), .in1(arith_1_result), .in2(shifter_1_shift_out), .in3(shifter_1_shift_out),
    .in4(shifter_1_shift_out), .in5(bit_extender_1_out), .in6(or_1_out), .in7(and_1_out),
    .in8(packed_ops_1_result), .in9(packed_ops_1_result), .in10(packed_ops_1_result),
    .in11(packed_ops_1_result), .out(Result), .sel(Selection));  // open: in12, in13, in14, in15, en
  Multiplexer multiplexer_2 (.in0(ArithSign), .in1(PackedSign), .out(Signed_OF), .sel(Selection[3]));  // open: en
  Multiplexer multiplexer_3 (.in0(ArithUN), .in1(PackedUN), .out(UNSigned), .sel(Selection[3]));  // open: en

  // Notes on the sheet:
  //   A
  //   B
  //   Select Wire
endmodule

// POps
module packed_ops (
  input  [15:0] InpA,
  input  [15:0] Inp_B,
  input  [1:0] Selection,
  output [15:0] Result,
  output UNsigned,
  output Signed
);

  wire adder_1_cout, adder_2_cout, signed_oflow_1_signed_overflow, signed_oflow_2_signed_overflow;
  wire [7:0] adder_1_out, adder_2_out, divider_1_out, divider_2_out, multiplier_1_out, multiplier_2_out,
       subtractor_1_out, subtractor_2_out;

  Multiplier multiplier_1 (.a(InpA[7:0]), .b(Inp_B[7:0]), .out(multiplier_1_out));  // open: cin, cout
  Multiplier multiplier_2 (.a(InpA[15:8]), .b(Inp_B[15:8]), .out(multiplier_2_out));  // open: cin, cout
  Divider divider_1 (.a(InpA[7:0]), .b(Inp_B[7:0]), .out(divider_1_out));  // open: upper, rem
  Divider divider_2 (.a(InpA[15:8]), .b(Inp_B[15:8]), .out(divider_2_out));  // open: upper, rem
  Adder adder_1 (.a(InpA[7:0]), .b(Inp_B[7:0]), .out(adder_1_out), .cout(adder_1_cout));  // open: cin
  Adder adder_2 (.a(InpA[15:8]), .b(Inp_B[15:8]), .out(adder_2_out), .cout(adder_2_cout));  // open: cin
  Subtractor subtractor_1 (.a(InpA[7:0]), .b(Inp_B[7:0]), .out(subtractor_1_out));  // open: bin, bout
  Subtractor subtractor_2 (.a(InpA[15:8]), .b(Inp_B[15:8]), .out(subtractor_2_out));  // open: bin, bout
  or or_1 (UNsigned, adder_1_cout, adder_2_cout);
  signed_oflow signed_oflow_1 (
    .InpA(InpA[7]), .InpB(Inp_B[7]), .Result(Result[7]), .Opselect(Selection[0]),
    .Signed_Overflow(signed_oflow_1_signed_overflow));
  signed_oflow signed_oflow_2 (
    .InpA(InpA[15]), .InpB(Inp_B[15]), .Result(Result[15]), .Opselect(Selection[0]),
    .Signed_Overflow(signed_oflow_2_signed_overflow));
  Multiplexer #(.select(2), .width(16)) multiplexer_1 (
    .in0({multiplier_2_out, multiplier_1_out}), .in1({divider_2_out, divider_1_out}),
    .in2({adder_2_out, adder_1_out}), .in3({subtractor_2_out, subtractor_1_out}), .out(Result),
    .sel(Selection));  // open: en
  or or_2 (Signed, signed_oflow_1_signed_overflow, signed_oflow_2_signed_overflow);

  // Other names for the same wires on the sheet: B1 = Inp_B[7]; B2 = Inp_B[15]; A1 = InpA[7]; A2 = InpA[15];
  //   R1 = Result[7]; R2 = Result[15]; SelBit = Selection[0]

  // Notes on the sheet:
  //   A lower
  //   B lower
  //   A upper
  //   B upper
endmodule

// Arith
module arith (
  input  [15:0] InpA,
  input  [15:0] InpB,
  input  Opselect,
  output \unsigned ,
  output [15:0] Result,
  output Signed_Overflow
);

  wire [15:0] adder_1_out, subtractor_1_out;

  Adder #(.width(16)) adder_1 (.a(InpA), .b(InpB), .out(adder_1_out), .cout(\unsigned ));  // open: cin
  Subtractor #(.width(16)) subtractor_1 (.a(InpA), .b(InpB), .out(subtractor_1_out));  // open: bin, bout
  Multiplexer #(.width(16)) multiplexer_1 (
    .in0(adder_1_out), .in1(subtractor_1_out), .out(Result), .sel(Opselect));  // open: en
  signed_oflow signed_oflow_1 (
    .InpA(InpA[15]), .InpB(InpB[15]), .Result(Result[15]), .Opselect(Opselect),
    .Signed_Overflow(Signed_Overflow));
endmodule

// Shifter
module shifter (
  input  [15:0] InpA,
  input  [15:0] InpB,
  input  [1:0] OpSelect,
  output [15:0] Shift_Out
);

  wire [15:0] shifter_1_out, shifter_2_out, shifter_3_out;

  Shifter #(.width(16), .shift("ar")) shifter_1 (.in(InpA), .\dist (InpB[3:0]), .out(shifter_1_out));
  Shifter #(.width(16)) shifter_2 (.in(InpA), .\dist (InpB[3:0]), .out(shifter_2_out));
  Shifter #(.width(16), .shift("lr")) shifter_3 (.in(InpA), .\dist (InpB[3:0]), .out(shifter_3_out));
  Multiplexer #(.select(2), .width(16)) multiplexer_1 (
    .in0(shifter_1_out), .in2(shifter_2_out), .in3(shifter_3_out), .out(Shift_Out), .sel(OpSelect));  // open: in1, en

  // Notes on the sheet:
  //   SRA
  //   SLL
  //   SRL
endmodule

// Signed
module signed_oflow (
  input  InpA,
  input  InpB,
  input  Result,
  input  Opselect,
  output Signed_Overflow
);

  wire and_1_out, and_2_out, and_3_out, and_4_out, not_1_out, not_2_out, not_3_out, not_4_out, not_5_out,
       not_6_out, or_1_out, or_2_out;

  not not_1 (not_1_out, InpA);
  not not_2 (not_2_out, InpB);
  not not_3 (not_3_out, Result);
  not not_4 (not_4_out, InpA);
  not not_5 (not_5_out, InpB);
  not not_6 (not_6_out, Result);
  and and_1 (and_1_out, not_1_out, not_2_out, Result);
  or or_1 (or_1_out, and_1_out, and_2_out);
  and and_2 (and_2_out, InpA, InpB, not_3_out);
  and and_3 (and_3_out, not_4_out, InpB, Result);
  or or_2 (or_2_out, and_3_out, and_4_out);
  and and_4 (and_4_out, InpA, not_5_out, not_6_out);
  Multiplexer multiplexer_1 (.in0(or_1_out), .in1(or_2_out), .out(Signed_Overflow), .sel(Opselect));  // open: en

  // Other names for the same wires on the sheet: A = InpA; B = InpB; R = Result

  // Notes on the sheet:
  //   Add Oflow
  //   Sub Oflow
endmodule
