// Logisim project Regfile.circ as structural Verilog: 1 circuit, main circuit main
module main (
  input  [1:0] Read_register_1,
  input  [1:0] Read_register_2,
  input  [1:0] write_register,
  input  [15:0] write_data,
  input  RegWrite,
  input  clock,
  output [15:0] Reg_0_Value,
  output [15:0] Reg_1_Value,
  output [15:0] Reg_2_Value,
  output [15:0] Reg_3_Value,
  output [15:0] Read_Data_1,
  output [15:0] Read_Data_2
);

  wire _0, _1, _2, _3;

  Register #(.width(16)) R0 (.D(write_data), .en(_0), .Q(Reg_0_Value), .clk(clock));  // open: clr
  Register #(.width(16)) R2 (.D(write_data), .en(_2), .Q(Reg_2_Value), .clk(clock));  // open: clr
  Demultiplexer #(.select(2), .disabled(0)) demultiplexer_1 (
    .out0(_0), .out1(_1), .out2(_2), .out3(_3), .in(RegWrite), .sel(write_register));  // open: en
  Register #(.width(16)) R1 (.D(write_data), .en(_1), .Q(Reg_1_Value), .clk(clock));  // open: clr
  Register #(.width(16)) R3 (.D(write_data), .en(_3), .Q(Reg_3_Value), .clk(clock));  // open: clr
  Multiplexer #(.select(2), .width(16)) multiplexer_1 (
    .in0(Reg_0_Value), .in1(Reg_1_Value), .in2(Reg_2_Value), .in3(Reg_3_Value), .out(Read_Data_1),
    .sel(Read_register_1));  // open: en
  Multiplexer #(.select(2), .width(16)) multiplexer_2 (
    .in0(Reg_0_Value), .in1(Reg_1_Value), .in2(Reg_2_Value), .in3(Reg_3_Value), .out(Read_Data_2),
    .sel(Read_register_2));  // open: en

  // Other names for the same wires on the sheet: _0O[15:0] = Reg_0_Value; _1O[15:0] = Reg_1_Value;
  //   _2O[15:0] = Reg_2_Value; _3O[15:0] = Reg_3_Value; clk = clock; Rd1[1:0] = Read_register_1;
  //   Rd2[1:0] = Read_register_2; RWr = RegWrite; WrD[15:0] = write_data; WrR[1:0] = write_register

  // Notes on the sheet:
  //   These are INPUTS to the circuit
  //   These are INPUTS to the circuit
  //   DO NOT CHANGE THE LOCATIONS OF THE INPUTS/OUTPUTS! IF YOU DO SO, YOU NEED TO MAKE SURE THE PINS ARE AT THE RIGHT PLACE!
  //   These are OUTPUTS to the circuit
  //   Yet again, the clock is not an actual clock, but an input, one that will be driven from a higher circuit
  //   These are OUTPUTS to the circuit
endmodule
