// Logisim project alu.circ as structural Verilog: 3 circuits, main circuit main
module main (
  input  [15:0] X,
  input  [15:0] Y,
  input  [3:0] switch__S,
  output signed_overflow,
  output [15:0] result,
  output equal
);

  wire ArithSign, comparator_1_lt, PackSign;
  wire [15:0] \and , Arith, lt, \or , pop, shift;

  arith_new arith_new_1 (.InpA(X), .InpB(Y), .Opselect(switch__S[0]), .Result(Arith), .Signed_Overflow(ArithSign));
  shifter shifter_1 (.InpA(X), .InpB(Y), .OpSelect(switch__S[1:0]), .Shift_Out(shift));
  Comparator #(.width(16)) comparator_1 (.a(X), .b(Y), .lt(comparator_1_lt));  // open: gt, eq
  assign \or  = X | Y;  // OR_Gate or_1, 16 bits wide
  assign \and  = X & Y;  // AND_Gate and_1, 16 bits wide
  packed_ops_new packed_ops_new_1 (.InpA(X), .Inp_B(Y), .Selection(switch__S[1:0]), .Result(pop), .Signed(PackSign));
  assign lt = {{15{1'b0}}, comparator_1_lt};  // Bit_Extender bit_extender_1
  Multiplexer #(.select(4), .width(16), .enable("false")) multiplexer_1 (
    .in0(Arith), .in1(Arith), .in2(shift), .in3(shift), .in4(shift), .in5(lt), .in6(\or ), .in7(\and ),
    .in8(pop), .in9(pop), .in10(pop), .in11(pop), .out(result), .sel(switch__S));  // open: in12, in13, in14, in15
  Multiplexer #(.disabled(0), .enable("false")) multiplexer_2 (
    .in0(ArithSign), .in1(PackSign), .out(signed_overflow), .sel(switch__S[3]));
  Comparator #(.width(16)) comparator_2 (.a(X), .b(Y), .eq(equal));  // open: gt, lt

  // Other names for the same wires on the sheet: S[3:0] = switch__S; S0 = switch__S[0]; S01[1:0] = switch__S[1:0];
  //   S3 = switch__S[3]

  // Notes on the sheet:
  //   These are INPUTS to your circuit
  //   This is an INPUT to your circuit
  //   DO NOT CHANGE THE LOCATIONS OF THE INPUTS/OUTPUTS! IF YOU DO SO, YOU NEED TO MAKE SURE THE PINS ARE AT THE RIGHT PLACE!
  //   These are OUTPUTS to your circuit
endmodule

// Arith
module arith_new (
  input  [15:0] InpA,
  input  [15:0] InpB,
  input  Opselect,
  output [15:0] Result,
  output Signed_Overflow
);

  wire [15:0] adder_1_out, subtractor_1_out;

  Adder #(.width(16)) adder_1 (.a(InpA), .b(InpB), .out(adder_1_out));  // open: cin, cout
  Subtractor #(.width(16)) subtractor_1 (.a(InpA), .b(InpB), .out(subtractor_1_out));  // open: bin, bout
  Multiplexer #(.width(16)) multiplexer_1 (
    .in0(adder_1_out), .in1(subtractor_1_out), .out(Result), .sel(Opselect));  // open: en
  signed_oflow signed_oflow_1 (
    .InpA(InpA[15]), .InpB(InpB[15]), .Result(Result[15]), .Opselect(Opselect),
    .Signed_Overflow(Signed_Overflow));
endmodule

// POps
module packed_ops_new (
  input  [15:0] InpA,
  input  [15:0] Inp_B,
  input  [1:0] Selection,
  output [15:0] Result,
  output Signed
);

  wire signed_oflow_1_signed_overflow, signed_oflow_2_signed_overflow;
  wire [7:0] adder_1_out, adder_2_out, divider_1_out, divider_2_out, multiplier_1_out, multiplier_2_out,
       subtractor_1_out, subtractor_2_out;

  Multiplier multiplier_1 (.a(InpA[7:0]), .b(Inp_B[7:0]), .out(multiplier_1_out));  // open: cin, cout
  Multiplier multiplier_2 (.a(InpA[15:8]), .b(Inp_B[15:8]), .out(multiplier_2_out));  // open: cin, cout
  Divider divider_1 (.a(InpA[7:0]), .b(Inp_B[7:0]), .out(divider_1_out));  // open: upper, rem
  Divider divider_2 (.a(InpA[15:8]), .b(Inp_B[15:8]), .out(divider_2_out));  // open: upper, rem
  Adder adder_1 (.a(InpA[7:0]), .b(Inp_B[7:0]), .out(adder_1_out));  // open: cin, cout
  Adder adder_2 (.a(InpA[15:8]), .b(Inp_B[15:8]), .out(adder_2_out));  // open: cin, cout
  Subtractor subtractor_1 (.a(InpA[7:0]), .b(Inp_B[7:0]), .out(subtractor_1_out));  // open: bin, bout
  Subtractor subtractor_2 (.a(InpA[15:8]), .b(Inp_B[15:8]), .out(subtractor_2_out));  // open: bin, bout
  signed_oflow signed_oflow_1 (
    .InpA(InpA[7]), .InpB(Inp_B[7]), .Result(Result[7]), .Opselect(Selection[0]),
    .Signed_Overflow(signed_oflow_1_signed_overflow));
  signed_oflow signed_oflow_2 (
    .InpA(InpA[15]), .InpB(Inp_B[15]), .Result(Result[15]), .Opselect(Selection[0]),
    .Signed_Overflow(signed_oflow_2_signed_overflow));
  Multiplexer #(.select(2), .width(16)) multiplexer_1 (
    .in0({multiplier_2_out, multiplier_1_out}), .in1({divider_2_out, divider_1_out}),
    .in2({adder_2_out, adder_1_out}), .in3({subtractor_2_out, subtractor_1_out}), .out(Result),
    .sel(Selection));  // open: en
  or or_1 (Signed, signed_oflow_1_signed_overflow, signed_oflow_2_signed_overflow);

  // Other names for the same wires on the sheet: B1 = Inp_B[7]; B2 = Inp_B[15]; A1 = InpA[7]; A2 = InpA[15];
  //   R1 = Result[7]; R2 = Result[15]; SelBit = Selection[0]

  // Notes on the sheet:
  //   A lower
  //   B lower
  //   A upper
  //   B upper
endmodule
