// Logisim project cpu.circ as structural Verilog: 7 circuits, main circuit main
module main (
  input  [15:0] From_Instr_Mem,
  input  clk,
  output [15:0] r0,
  output [15:0] r1,
  output [15:0] r2,
  output [15:0] r3,
  output [15:0] Display_0,
  output [15:0] Display_1,
  output [15:0] To_Instr_Mem,
  output [15:0] Data_Mem_Data,
  output [15:0] Data_Mem_Addr,
  output Data_Mem_Write
);

  wire addi, ALU_signed_overflow, ALUSrc, and_1_out, and_2_out, andi, beq, bne, branch, disp, equ, ExtOp,
       i_type, j, j_type, jal, jr, lui, lw, MemtoReg, not_1_out, not_2_out, ori, PC_skip, r_type, RegDst,
       RegWr, sw;
  wire [1:0] multiplexer_2_out, multiplexer_3_out;
  wire [3:0] ALUCtrl;
  wire [5:0] funct;
  wire [7:6] imm;
  wire [15:0] and_3_out, bit_extender_1_out, controlled_buffer_1_out, ExtImm, ExtImm_t, jaddr, luiImm,
       multiplexer_1_out, multiplexer_4_out, multiplexer_5_out, multiplexer_6_out, multiplexer_8_out,
       or_2_out, pc1, RdR1, RdR2, shifter_1_out, undriven, WriteData;
  wire [15:8] instr;

  type_check type_check_1 (.opcode(instr[15:12]), .out_2(r_type), .out_3(j_type), .out_4(i_type));
  Hex_Digit_Display hex_digit_display_1 (.value(Display_0[15:12]));  // open: dp
  Hex_Digit_Display hex_digit_display_2 (.value(Display_0[7:4]));  // open: dp
  Hex_Digit_Display hex_digit_display_3 (.value(Display_0[11:8]));  // open: dp
  Hex_Digit_Display hex_digit_display_4 (.value(Display_0[3:0]));  // open: dp
  pipleline pipleline_1 (
    .iMem(From_Instr_Mem), .iMem_Out({instr, imm, funct}), .clk(clk), .jump(j_type), .branch(branch));
  Control control_1 (
    .opcode(instr[15:12]), .funct_code(funct), .RegWr(RegWr), .RegDst(RegDst), .ALUSrc(ALUSrc),
    .ExtOp(ExtOp), .inst_skip(PC_skip), .MemtoReg(MemtoReg), .MemWrite(Data_Mem_Write), .ALUCtr(ALUCtrl),
    .jal(jal), .j(j), .jr(jr), .beq(beq), .addi(addi), .andi(andi), .ori(ori), .bne(bne), .sw(sw), .lui(lui),
    .lw(lw), .disp(disp));
  Hex_Digit_Display hex_digit_display_5 (.value(Display_1[11:8]));  // open: dp
  Hex_Digit_Display hex_digit_display_6 (.value(Display_1[15:12]));  // open: dp
  display u_display_1 (
    .opcode(instr[15:12]), .RdR1(RdR1), .RdR2(RdR2), .imm({imm, funct}), .display_1(Display_0),
    .display_2(Display_1), .clk(clk));
  Multiplexer #(.width(16), .enable("false")) multiplexer_1 (
    .in0(pc1), .in1(jaddr), .out(multiplexer_1_out), .sel(j_type));
  Multiplexer #(.width(2), .enable("false")) multiplexer_2 (
    .in0(instr[9:8]), .in1(imm), .out(multiplexer_2_out), .sel(RegDst));
  Hex_Digit_Display hex_digit_display_7 (.value(Display_1[3:0]));  // open: dp
  Hex_Digit_Display hex_digit_display_8 (.value(Display_1[7:4]));  // open: dp
  Shifter #(.width(16)) shifter_1 (.in(ExtImm_t), .\dist (4'b0010), .out(shifter_1_out));
  Multiplexer #(.width(2), .enable("false")) multiplexer_3 (
    .in0(2'b11), .in1(multiplexer_2_out), .out(multiplexer_3_out), .sel(jal));
  Adder #(.width(16)) adder_1 (.a(To_Instr_Mem), .b(shifter_1_out));  // open: out, cin, cout
  Multiplexer #(.width(16), .enable("false")) multiplexer_4 (
    .in0(WriteData), .in1(To_Instr_Mem), .out(multiplexer_4_out), .sel(jal));
  assign controlled_buffer_1_out = Data_Mem_Write ? RdR2 : 16'bz;  // Controlled_Buffer controlled_buffer_1
  Multiplexer #(.width(16), .enable("false")) multiplexer_5 (
    .in0(multiplexer_1_out), .in1(undriven), .out(multiplexer_5_out), .sel(branch));
  Register #(.width(16)) register_1 (.D(multiplexer_5_out), .Q(To_Instr_Mem), .clk(clk));  // open: en, clr
  Regfile_main main (
    .Read_register_1(instr[11:10]), .Read_register_2(instr[9:8]), .write_register(multiplexer_3_out),
    .write_data(multiplexer_4_out), .Reg_0_Value(r0), .Reg_1_Value(r1), .Reg_2_Value(r2), .Reg_3_Value(r3),
    .RegWrite(RegWr), .clock(clk), .Read_Data_1(RdR1), .Read_Data_2(RdR2));
  RAM #(.addrWidth(16), .dataWidth(16), .bus("separate")) ram_1 (
    .addr(Data_Mem_Addr), .din(controlled_buffer_1_out), .data(Data_Mem_Data), .str(Data_Mem_Write),
    .sel(1'b1), .clk(clk), .ld(not_1_out), .clr(1'b0));
  not not_1 (not_1_out, Data_Mem_Write);
  Adder #(.width(16)) adder_2 (.a(To_Instr_Mem), .b(16'h1), .out(pc1));  // open: cin, cout
  Multiplexer #(.width(16), .enable("false")) multiplexer_6 (
    .in0(Data_Mem_Addr), .in1(luiImm), .out(multiplexer_6_out), .sel(lui));
  and and_1 (and_1_out, bne, not_2_out);
  not not_2 (not_2_out, equ);
  and and_2 (and_2_out, beq, equ);
  Multiplexer #(.width(16), .enable("false")) multiplexer_7 (
    .in0(Data_Mem_Data), .in1(multiplexer_6_out), .out(WriteData), .sel(MemtoReg));
  Extender extender_1 (.Input({imm, funct}), .Result(ExtImm_t), .ExtOp(ExtOp));
  or or_1 (branch, and_1_out, and_2_out);
  Shifter #(.width(16)) shifter_2 (.in(ExtImm), .\dist (4'b1000), .out(luiImm));
  Multiplexer #(.width(16), .enable("false")) multiplexer_8 (
    .in0(RdR2), .in1(ExtImm_t), .out(multiplexer_8_out), .sel(ALUSrc));
  assign and_3_out = To_Instr_Mem & 16'hf000;  // AND_Gate and_3, 16 bits wide
  assign bit_extender_1_out = {{4{1'b0}}, {instr[11:10], imm, instr[9:8], funct}};  // Bit_Extender bit_extender_1
  LED OFlow (.in(ALU_signed_overflow));
  alu_main ALU (
    .switch__S(ALUCtrl), .X(RdR1), .equal(equ), .result(Data_Mem_Addr),
    .signed_overflow(ALU_signed_overflow), .Y(multiplexer_8_out));
  assign or_2_out = and_3_out | bit_extender_1_out;  // OR_Gate or_2, 16 bits wide
  Multiplexer #(.width(16), .enable("false")) multiplexer_9 (.in0(or_2_out), .in1(RdR1), .out(jaddr), .sel(jr));

  // Other names for the same wires on the sheet: ALUOut[15:0] = Data_Mem_Addr; d0[15:0] = Display_0;
  //   d1[15:0] = Display_1; DMD[15:0] = Data_Mem_Data; from[15:0] = From_Instr_Mem; imm[5:0] = funct;
  //   instr[7:0] = {imm, funct}; j_jal[11:0] = {instr[11:10], imm, instr[9:8], funct}; rd[1:0] = imm;
  //   opcode[3:0] = instr[15:12]; rt[1:0] = instr[9:8]; rs[1:0] = instr[11:10]; MemWr = Data_Mem_Write;
  //   pc[15:0] = To_Instr_Mem

  // Notes on the sheet:
  //   PC Out
  //   Decode
  //   -LINING
  //   Branches & Jumps
  //   These are OUTPUTS to the circuit
  //   Registers
  //   jal work for $r3
  //   RAM
  //   Memory
  //   PC+1 (eq PC+4)
endmodule

module Control (
  input  [3:0] opcode,
  input  [5:0] funct_code,
  output RegWr,
  output RegDst,
  output ALUSrc,
  output ExtOp,
  output inst_skip,
  output MemtoReg,
  output MemWrite,
  output [3:0] ALUCtr,
  output jal,
  output j,
  output jr,
  output beq,
  output addi,
  output andi,
  output ori,
  output bne,
  output sw,
  output lui,
  output lw,
  output disp
);

  wire or_1_out, rtype;
  wire [3:0] multiplexer_1_out;

  Multiplexer #(.select(4), .width(4), .enable("false")) multiplexer_1 (
    .in0(4'b0000), .in1(4'b0000), .in2(4'b0000), .in3(4'b0000), .in4(4'b0001), .in5(4'b0000), .in6(4'b0111),
    .in7(4'b0110), .in8(4'b0001), .in9(4'b0000), .in10(4'b0010), .in11(4'b0000), .in12(4'b0000),
    .in13(4'b0000), .in14(4'b0000), .in15(4'b0000), .out(multiplexer_1_out), .sel(opcode));
  not not_1 (ExtOp, or_1_out);
  or or_1 (or_1_out, addi, ori, lui, disp);
  nor nor_1 (RegWr, inst_skip, MemWrite, disp);
  or or_2 (inst_skip, beq, bne, jal, j, jr);
  Multiplexer #(.width(4), .enable("false")) multiplexer_2 (
    .in0(funct_code[3:0]), .in1(multiplexer_1_out), .out(ALUCtr), .sel(ALUSrc));
  opcode_instr opcode_instr_1 (
    .opcode(opcode), .rtype(rtype), .jal(jal), .j(j), .jr(jr), .beq(beq), .addi(addi), .andi(andi),
    .ori(ori), .bne(bne), .sw(MemWrite), .lui(lui), .lw(lw), .disp(disp));
  not not_2 (ALUSrc, rtype);

  assign MemtoReg = lw;
  assign RegDst = ALUSrc;
  assign sw = MemWrite;

  // Other names for the same wires on the sheet: alu[3:0] = ALUCtr; funct[5:0] = funct_code; notR = ALUSrc;
  //   skip_instr = inst_skip

  // Notes on the sheet:
  //   Opcode or funct in ALU?
endmodule

// Ext?
module Extender (
  input  [7:0] Input,
  input  ExtOp,
  output [15:0] Result
);

  wire [15:0] bit_extender_1_out, bit_extender_2_out;

  assign bit_extender_1_out = {{8{1'b0}}, Input};  // Bit_Extender bit_extender_1
  Multiplexer #(.width(16), .enable("false")) multiplexer_1 (
    .in0(bit_extender_1_out), .in1(bit_extender_2_out), .out(Result), .sel(ExtOp));
  assign bit_extender_2_out = {{8{Input[7]}}, Input};  // Bit_Extender bit_extender_2

  // Notes on the sheet:
  //   Immediate
endmodule

module pipleline (
  input  [15:0] iMem,
  input  clk,
  input  branch,
  input  jump,
  output [15:0] iMem_Out
);

  wire beq_bne, j_type, or_1_out, or_2_out;
  wire [15:0] multiplexer_1_out, undriven;

  Multiplexer #(.width(16), .enable("false")) multiplexer_1 (
    .in0(iMem), .in1({16{1'b0}}), .out(multiplexer_1_out), .sel(or_1_out));
  or or_1 (or_1_out, branch, jump);
  Multiplexer #(.width(16)) multiplexer_2 (.in0(undriven), .in1({16{1'b0}}), .sel(or_2_out));  // open: out, en
  or or_2 (or_2_out, beq_bne, j_type);
  Register #(.width(16)) register_1 (.D(multiplexer_1_out), .Q(iMem_Out), .clk(clk));  // open: en, clr
endmodule

module display (
  input  [3:0] opcode,
  input  [15:0] RdR1,
  input  [15:0] RdR2,
  input  [7:0] imm,
  input  clk,
  output [15:0] display_1,
  output [15:0] display_2
);

  wire and_1_out, and_2_out, comparator_1_eq, comparator_2_eq, comparator_3_eq;

  Comparator #(.width(4)) comparator_1 (.a(opcode), .b(4'b0000), .eq(comparator_1_eq));  // open: gt, lt
  Comparator comparator_2 (.a({8{1'b0}}), .b(imm), .eq(comparator_2_eq));  // open: gt, lt
  Register #(.width(16)) register_1 (.D(RdR1), .en(and_1_out), .Q(display_1), .clk(clk));  // open: clr
  and and_1 (and_1_out, comparator_1_eq, comparator_2_eq);
  and and_2 (and_2_out, comparator_1_eq, comparator_3_eq);
  Comparator comparator_3 (.a(8'h1), .b(imm), .eq(comparator_3_eq));  // open: gt, lt
  Register #(.width(16)) register_2 (.D(RdR2), .en(and_2_out), .Q(display_2), .clk(clk));  // open: clr

  // Other names for the same wires on the sheet: d0[15:0] = display_1; d1[15:0] = display_2
endmodule

// Control
module opcode_instr (
  input  [3:0] opcode,
  output jal,
  output j,
  output jr,
  output rtype,
  output beq,
  output addi,
  output andi,
  output ori,
  output bne,
  output sw,
  output lui,
  output lw,
  output disp
);

  wire not_1_out, not_2_out, not_3_out, not_4_out, not_5_out, not_6_out, not_7_out, not_8_out, not_9_out,
       not_10_out, not_11_out, not_12_out, not_13_out, not_14_out, not_15_out, not_16_out, not_17_out,
       not_18_out, not_19_out, not_20_out, not_21_out, not_22_out;

  not not_1 (not_1_out, opcode[2]);
  not not_2 (not_2_out, opcode[3]);
  and and_1 (rtype, not_2_out, not_1_out, not_4_out, not_3_out);
  not not_3 (not_3_out, opcode[0]);
  not not_4 (not_4_out, opcode[1]);
  not not_5 (not_5_out, opcode[3]);
  not not_6 (not_6_out, opcode[2]);
  not not_7 (not_7_out, opcode[1]);
  not not_8 (not_8_out, opcode[3]);
  not not_9 (not_9_out, opcode[2]);
  not not_10 (not_10_out, opcode[0]);
  not not_11 (not_11_out, opcode[3]);
  not not_12 (not_12_out, opcode[2]);
  not not_13 (not_13_out, opcode[3]);
  not not_14 (not_14_out, opcode[1]);
  not not_15 (not_15_out, opcode[0]);
  not not_16 (not_16_out, opcode[1]);
  not not_17 (not_17_out, opcode[0]);
  and and_2 (ori, opcode[2], opcode[1], opcode[0]);
  not not_18 (not_18_out, opcode[2]);
  not not_19 (not_19_out, opcode[1]);
  not not_20 (not_20_out, opcode[0]);
  not not_21 (not_21_out, opcode[1]);
  not not_22 (not_22_out, opcode[0]);
  and and_3 (lw, opcode[3], opcode[1], opcode[0]);
  and and_4 (disp, opcode[3], opcode[2]);
  and and_5 (jal, not_5_out, not_6_out, not_7_out, opcode[0]);
  and and_6 (j, not_8_out, not_9_out, opcode[1], not_10_out);
  and and_7 (jr, not_11_out, not_12_out, opcode[1], opcode[0]);
  and and_8 (beq, not_13_out, opcode[2], not_14_out, not_15_out);
  and and_9 (addi, opcode[2], not_16_out, opcode[0]);
  and and_10 (andi, opcode[2], opcode[1], not_17_out);
  and and_11 (bne, opcode[3], not_18_out, not_19_out, not_20_out);
  and and_12 (sw, opcode[3], not_21_out, opcode[0]);
  and and_13 (lui, opcode[3], opcode[1], not_22_out);

  // Notes on the sheet:
  //   combinational analysis feature
  //   3
  //   GIVES THE FUNCT NAME
  //   Built using logisim
  //   2
  //   1
  //   0
endmodule

module type_check (
  input  [3:0] opcode,
  output out_2,
  output out_3,
  output out_4
);

  wire comparator_2_lt, not_1_out;

  Comparator #(.width(4), .mode("unsigned")) comparator_1 (.a(opcode), .b(4'b0000), .eq(out_2));  // open: gt, lt
  not not_1 (not_1_out, out_2);
  and and_1 (out_3, not_1_out, comparator_2_lt);
  Comparator #(.width(4), .mode("unsigned")) comparator_2 (
    .a(opcode), .b(4'b0100), .lt(comparator_2_lt));  // open: gt, eq
  nor nor_1 (out_4, out_2, out_3);

  // Other names for the same wires on the sheet: itype = out_4; jtype = out_3; rtype = out_2
endmodule
